# Fritzing sketch cable release circuit (saved by Fritzing 0.9.4)

parts:
  Mod1 = Raspberry Pi Pico
  Part1 = 14-segment LED Alphanumeric Backpack [part_number=1911]
  RE1 = KY-040 Rotary encoder [package=THT]
  BUTTON1 = Arcade Button (blue)
  BAT1 = Battery Holders [package=battery-aaa]
  BAT2 = Battery Holders [package=battery-aaa]
  BAT3 = Battery Holders [package=battery-aaa]
  BAT4 = Battery Holders [package=battery-aaa]
  S2 = Taiway 100-SP-X-T1 SPDT Miniature Toggle Switch [part_number=100-SP-X-T1-0-0-B1-M2 package=THT]
  U2 = LM2596 step down module
  BAT5 = Battery Holders [package=battery-aaa]
  J1 = Basic Servo

nets:
  N1: Mod1.pin_1, Part1.SDA
  N2: Mod1.pin_2, Part1.SCL
  GND: Mod1.pin_8, Mod1.pin_18, Mod1.pin_28, Part1.GND, RE1.GND, BUTTON1.no_name_yet#2
  N3: Mod1.pin_11, RE1.CLK
  N4: Mod1.pin_12, RE1.DT
  N5: Mod1.pin_21, RE1.SW
  N6: Mod1.pin_29, BUTTON1.no_name_yet#1
  N7: Mod1.pin_34, J1.pulse
  N8: Mod1.pin_36, Part1.VI2C, RE1.Vcc
  N9: Mod1.pin_39, Part1.VDD
  N10: Mod1.pin_40, U2.OUT+
  N11: BAT1.+, BAT2.-
  N12: BAT2.+, BAT3.-
  N13: BAT3.+, BAT5.-
  N14: BAT4.-, BAT5.+
  N15: BAT4.+, S2.COM
  N16: S2.L2, U2.IN+, J1.vcc
  N17: U2.IN-, U2.OUT-

custom parts:
  Raspberry Pi Pico: Raspberry Pi Pico. Based around the RP2040 microcontroller the Pico is a low cost microcontroller device bringing Raspberry Pi quality, cost, and easy of use to the microcontroller space. Jan 2021, Split part in to two versions: tht (this one) and SMD. This one will drill holes for a .1 in header in pcb to allow plugging in the module as well as providing pads to solder the module to the top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
  14-segment LED Alphanumeric Backpack: This is a nice, bright alphanumeric display that shows letters and numbers. It's super bright and designed for viewing from distances up to 23 feet (7 meters) away. Four digits with 14 segments on a black surface and we give you a set of two alphanumeric displays as well as a driver board so you can make a clock or a four letter word. Like our other LED backpacks, these are end-to-end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
  KY-040 Rotary encoder: KY-040 Rotary Encoder with switch on breakout borad from AZ Delivery
  Arcade Button (blue): Adafruit Arcade Button (blue)
  LM2596 step down module: LM2596 DC-DC step down power supply module 3 A.
